// Logisim project 8-bit TTL Cpu.circ as structural Verilog: 3 circuits, main circuit main
module main (
);

  wire ALU___74LS181_cn_4, ALU_C, ALU_F0, ALU_F1, ALU_F2, ALU_F3, ALU_M, ALU_OUT_to_REG_IN, and_1_out,
       and_2_out, and_3_out, and_4_out, and_5_out, and_6_out, and_7_out, and_8_out, and_9_out, and_10_out,
       and_11_out, and_12_out, CLK_B, clock_1_out, d_ff_1_q, decoder_1_out4, decoder_2_out0, decoder_2_out1,
       decoder_2_out4, decoder_2_out5, decoder_3_out0, decoder_3_out1, decoder_3_out4, decoder_3_out5,
       EN_MEM, EN_REG_CLK, Execute, Fetch_1, Fetch_2, Fetch_3, Fetch_Any, IR_ADDR_to_MEM_ADDR, IR_ADDR_to_PC,
       IR_DATA_to_REG_IN, MEM_DATA_to_REG_IN, MEM_READ, nand_1_out, or_1_out, or_2_out, OUT_REG_to_REG_IN,
       PC_Next, Reset, RR3_to_MEM_ADDR;
  wire [2:0] counter_1_q, R1_Addr, R2_Addr;
  wire [5:0] OPCODE;
  wire [7:0] ALU___74LS181_2_f0, ALU_A_IN, ALU_B_IN, B_q, E_q, F_q, ram_1_data, REG_IN;
  wire [11:0] adder_1_out, controlled_buffer_2_out, controlled_buffer_4_out, IR_Addr, PC_q;

  Counter #(.width(3), .max('h7)) counter_1 (
    .count(1'b1), .Q(counter_1_q), .clk(nand_1_out), .clr(or_1_out));  // open: load, D, carry
  Clock clock_1 (.out(clock_1_out));
  Decoder #(.select(3)) decoder_1 (
    .out0(Fetch_1), .out1(Fetch_2), .out2(Fetch_3), .out3(Execute), .out4(decoder_1_out4), .sel(counter_1_q),
    .en(1'b1));  // open: out5, out6, out7
  or or_1 (or_1_out, decoder_1_out4, Reset);
  and and_1 (and_1_out, nand_1_out, clock_1_out);
  D_Flip_Flop d_ff_1 (.clk(and_1_out), .D(1'b1), .Q(d_ff_1_q), .reset(Reset));  // open: Qn, preset, en
  not not_1 (Fetch_Any, Execute);
  not not_2 (CLK_B, nand_1_out);
  nand nand_1 (nand_1_out, clock_1_out, d_ff_1_q);
  Instruction_Decoder Instruction_Decoder (
    .A5(OPCODE[5]), .A4(OPCODE[4]), .A3(OPCODE[3]), .A2(OPCODE[2]), .A1(OPCODE[1]), .A0(OPCODE[0]),
    .IR_DATA_to_REG_IN(IR_DATA_to_REG_IN), .EN_REG_CLK(EN_REG_CLK), .OUT_REG_to_REG_IN(OUT_REG_to_REG_IN),
    .IR_ADDR_to_MEM_ADDR(IR_ADDR_to_MEM_ADDR), .EN_MEM(EN_MEM), .MEM_READ(MEM_READ),
    .MEM_DATA_to_REG_IN(MEM_DATA_to_REG_IN), .RR3_to_MEM_ADDR(RR3_to_MEM_ADDR),
    .ALU_OUT_to_REG_IN(ALU_OUT_to_REG_IN), .IR_ADDR_to_PC(IR_ADDR_to_PC));  // open: Z_FLAG_to_IR_ADDR_to_PC, R1_to_MEM_DATA
  Instruction_Decoder__cont Instruction_Decoder__cont (
    .A5(OPCODE[5]), .A4(OPCODE[4]), .A3(OPCODE[3]), .A2(OPCODE[2]), .A1(OPCODE[1]), .A0(OPCODE[0]),
    .ALU_F3(ALU_F3), .ALU_F2(ALU_F2), .ALU_F1(ALU_F1), .ALU_F0(ALU_F0), .ALU_M(ALU_M), .ALU_C(ALU_C));
  _74181 ALU___74LS181 (
    .S3(ALU_F3), .S2(ALU_F2), .S1(ALU_F1), .S0(ALU_F0), .B3(ALU_B_IN[7]), .A3(ALU_A_IN[7]), .B2(ALU_B_IN[6]),
    .A2(ALU_A_IN[6]), .B1(ALU_B_IN[5]), .A1(ALU_A_IN[5]), .B0(ALU_B_IN[4]), .A0(ALU_A_IN[4]), .M(ALU_M),
    .Cn(ALU_C), .Cn_4(ALU___74LS181_cn_4), .F3(ALU___74LS181_2_f0[7]), .F2(ALU___74LS181_2_f0[6]),
    .F1(ALU___74LS181_2_f0[5]), .F0(ALU___74LS181_2_f0[4]));  // open: G, P, A_B
  _74181 ALU___74LS181_2 (
    .S3(ALU_F3), .S2(ALU_F2), .S1(ALU_F1), .S0(ALU_F0), .B3(ALU_B_IN[3]), .A3(ALU_A_IN[3]), .B2(ALU_B_IN[2]),
    .A2(ALU_A_IN[2]), .B1(ALU_B_IN[1]), .A1(ALU_A_IN[1]), .B0(ALU_B_IN[0]), .A0(ALU_A_IN[0]), .M(ALU_M),
    .Cn(ALU___74LS181_cn_4), .F3(ALU___74LS181_2_f0[3]), .F2(ALU___74LS181_2_f0[2]),
    .F1(ALU___74LS181_2_f0[1]), .F0(ALU___74LS181_2_f0[0]));  // open: G, Cn_4, P, A_B
  Adder #(.width(12)) adder_1 (.a(controlled_buffer_4_out), .b(12'h1), .out(adder_1_out), .cin(1'b0));  // open: cout
  and and_2 (and_2_out, IR_ADDR_to_PC, Execute);
  assign REG_IN = ALU_OUT_to_REG_IN ? ALU___74LS181_2_f0 : 8'bz;  // Controlled_Buffer controlled_buffer_1
  assign controlled_buffer_2_out = Fetch_Any ? adder_1_out : 12'bz;  // Controlled_Buffer controlled_buffer_2
  assign controlled_buffer_2_out = and_2_out ? IR_Addr : 12'bz;  // Controlled_Buffer controlled_buffer_3
  and and_3 (and_3_out, and_2_out, CLK_B);
  Button button_1 (.out(Reset));
  Decoder #(.select(3)) decoder_2 (
    .out0(decoder_2_out0), .out1(decoder_2_out1), .out4(decoder_2_out4), .out5(decoder_2_out5),
    .sel(R1_Addr), .en(1'b1));  // open: out2, out3, out6, out7
  Register #(.width(12)) PC (.D(controlled_buffer_2_out), .Q(PC_q), .clk(or_2_out), .clr(Reset));  // open: en
  or or_2 (or_2_out, and_3_out, PC_Next);
  and and_4 (and_4_out, IR_ADDR_to_MEM_ADDR, Execute);
  assign controlled_buffer_4_out = Fetch_Any ? PC_q : 12'bz;  // Controlled_Buffer controlled_buffer_4
  assign controlled_buffer_4_out = and_4_out ? IR_Addr : 12'bz;  // Controlled_Buffer controlled_buffer_5
  assign REG_IN = IR_DATA_to_REG_IN ? IR_Addr[7:0] : 8'bz;  // Controlled_Buffer controlled_buffer_6
  and and_5 (and_5_out, CLK_B, Execute, EN_REG_CLK);
  RAM #(.addrWidth(12), .bus("asynch")) ram_1 (
    .addr(controlled_buffer_4_out), .data(ram_1_data), .sel(1'b1), .ld(1'b1));  // open: clr
  assign REG_IN = MEM_DATA_to_REG_IN ? ram_1_data : 8'bz;  // Controlled_Buffer controlled_buffer_7
  and and_6 (and_6_out, decoder_2_out0, and_5_out);
  and and_7 (and_7_out, decoder_2_out1, and_5_out);
  and and_8 (and_8_out, decoder_2_out4, and_5_out);
  and and_9 (and_9_out, decoder_2_out5, and_5_out);
  Register A (.D(REG_IN), .Q(ALU_A_IN), .clk(and_6_out), .clr(Reset));  // open: en
  Register B (.D(REG_IN), .Q(B_q), .clk(and_7_out), .clr(Reset));  // open: en
  Register E (.D(REG_IN), .Q(E_q), .clk(and_8_out), .clr(Reset));  // open: en
  Register F (.D(REG_IN), .Q(F_q), .clk(and_9_out), .clr(Reset));  // open: en
  and and_10 (and_10_out, Fetch_3, CLK_B);
  and and_11 (and_11_out, Fetch_2, CLK_B);
  and and_12 (and_12_out, Fetch_1, CLK_B);
  and and_13 (PC_Next, CLK_B, Fetch_Any);
  Register IR_3 (.D(ram_1_data), .Q(IR_Addr[7:0]), .clk(and_10_out), .clr(Reset));  // open: en
  Register IR_2 (.D(ram_1_data), .Q({R1_Addr[0], R2_Addr, IR_Addr[11:8]}), .clk(and_11_out), .clr(Reset));  // open: en
  Register IR_1 (.D(ram_1_data), .Q({OPCODE, R1_Addr[2:1]}), .clk(and_12_out), .clr(Reset));  // open: en
  assign REG_IN = OUT_REG_to_REG_IN ? ALU_B_IN : 8'bz;  // Controlled_Buffer controlled_buffer_8
  assign ALU_B_IN = decoder_3_out0 ? ALU_A_IN : 8'bz;  // Controlled_Buffer controlled_buffer_9
  assign ALU_B_IN = decoder_3_out1 ? B_q : 8'bz;  // Controlled_Buffer controlled_buffer_10
  assign ALU_B_IN = decoder_3_out4 ? E_q : 8'bz;  // Controlled_Buffer controlled_buffer_11
  assign ALU_B_IN = decoder_3_out5 ? F_q : 8'bz;  // Controlled_Buffer controlled_buffer_12
  Decoder #(.select(3)) decoder_3 (
    .out0(decoder_3_out0), .out1(decoder_3_out1), .out4(decoder_3_out4), .out5(decoder_3_out5),
    .sel(R2_Addr), .en(1'b1));  // open: out2, out3, out6, out7

  // Other names for the same wires on the sheet: IR_Data[7:0] = IR_Addr[7:0]

  // Notes on the sheet:
  //   Equiv to 74HCT4017
  //   This odd block is just to make sure the initial state on reset will always be Fetch-1 High and CLK-B Low
  //   JACA-2 - 8-bit Homebrew CPU
  //   v. 0.7.0
  //   https://hackaday.io/project/24511-jaca-1-homebrew-cpu
  //   Most significant byte
  //   RAM
  //   REG_IN
  //   Least significant byte
  //   This is the only 74HCT244, all other are the 3 state output of the registers
  //   =RR3 Hi
endmodule

module Instruction_Decoder (
  input  A5,
  input  A4,
  input  A3,
  input  A2,
  input  A1,
  input  A0,
  output IR_DATA_to_REG_IN,
  output EN_REG_CLK,
  output OUT_REG_to_REG_IN,
  output IR_ADDR_to_MEM_ADDR,
  output EN_MEM,
  output MEM_READ,
  output MEM_DATA_to_REG_IN,
  output RR3_to_MEM_ADDR,
  output ALU_OUT_to_REG_IN,
  output IR_ADDR_to_PC,
  output Z_FLAG_to_IR_ADDR_to_PC,
  output R1_to_MEM_DATA
);

  wire and_1_out, and_2_out, and_4_out, and_5_out, and_6_out, and_7_out, and_9_out, and_10_out, and_11_out,
       and_12_out, and_13_out, and_14_out, and_15_out, and_16_out, and_17_out, and_18_out, and_19_out,
       and_20_out, and_21_out, and_22_out, and_23_out, and_24_out, and_25_out, and_26_out, not_1_out,
       not_2_out, not_3_out, not_4_out, not_5_out, not_6_out, not_7_out, not_8_out, not_9_out, not_10_out,
       not_11_out, not_12_out, not_13_out, not_14_out, not_15_out, not_16_out, not_17_out, not_18_out,
       not_19_out, not_20_out, not_21_out, not_22_out, not_23_out, not_24_out, not_25_out, not_26_out,
       not_27_out, not_28_out, not_29_out, not_30_out, not_31_out, not_32_out, not_33_out, not_34_out,
       not_35_out, not_36_out, not_37_out, not_38_out, not_39_out;

  not not_1 (not_1_out, A3);
  not not_2 (not_2_out, A2);
  not not_3 (not_3_out, A1);
  not not_4 (not_4_out, A3);
  not not_5 (not_5_out, A2);
  not not_6 (not_6_out, A0);
  not not_7 (not_7_out, A3);
  not not_8 (not_8_out, A2);
  not not_9 (not_9_out, A1);
  not not_10 (not_10_out, A3);
  not not_11 (not_11_out, A2);
  not not_12 (not_12_out, A0);
  not not_13 (not_13_out, A3);
  not not_14 (not_14_out, A2);
  not not_15 (not_15_out, A3);
  not not_16 (not_16_out, A2);
  not not_17 (not_17_out, A3);
  not not_18 (not_18_out, A1);
  not not_19 (not_19_out, A0);
  not not_20 (not_20_out, A3);
  not not_21 (not_21_out, A3);
  not not_22 (not_22_out, A3);
  not not_23 (not_23_out, A2);
  not not_24 (not_24_out, A3);
  not not_25 (not_25_out, A1);
  not not_26 (not_26_out, A0);
  not not_27 (not_27_out, A3);
  not not_28 (not_28_out, A1);
  not not_29 (not_29_out, A0);
  not not_30 (not_30_out, A3);
  not not_31 (not_31_out, A3);
  not not_32 (not_32_out, A2);
  not not_33 (not_33_out, A1);
  not not_34 (not_34_out, A2);
  not not_35 (not_35_out, A0);
  not not_36 (not_36_out, A1);
  not not_37 (not_37_out, A0);
  not not_38 (not_38_out, A1);
  not not_39 (not_39_out, A0);
  and and_1 (and_1_out, A3, A2, A0);
  and and_2 (and_2_out, A3, A2, A1);
  and and_3 (IR_DATA_to_REG_IN, not_1_out, not_2_out, not_3_out, A0);
  and and_4 (and_4_out, not_4_out, A0);
  and and_5 (and_5_out, not_5_out, A1, not_6_out);
  and and_6 (and_6_out, not_7_out, A2);
  and and_7 (and_7_out, A3, not_8_out, not_9_out);
  and and_8 (OUT_REG_to_REG_IN, not_10_out, not_11_out, A1, not_12_out);
  and and_9 (and_9_out, not_13_out, not_14_out, A1, A0);
  and and_10 (and_10_out, A3, A2, A0);
  and and_11 (and_11_out, not_15_out, not_16_out, A1, A0);
  and and_12 (and_12_out, not_17_out, A2, not_18_out, not_19_out);
  and and_13 (and_13_out, A3, A2, A0);
  and and_14 (and_14_out, A3, A2, A1);
  and and_15 (and_15_out, not_20_out, A1);
  and and_16 (and_16_out, not_21_out, A2);
  and and_17 (and_17_out, not_22_out, not_23_out, A1, A0);
  and and_18 (and_18_out, not_24_out, A2, not_25_out, not_26_out);
  and and_19 (and_19_out, not_27_out, A2, not_28_out, not_29_out);
  and and_20 (and_20_out, A3, A2, A1);
  and and_21 (and_21_out, not_30_out, A2, A0);
  and and_22 (and_22_out, not_31_out, A2, A1);
  and and_23 (and_23_out, A3, not_32_out, not_33_out);
  and and_24 (and_24_out, A3, not_34_out, not_35_out);
  and and_25 (and_25_out, A3, A1, A0);
  and and_26 (and_26_out, A3, A2, not_36_out, not_37_out);
  and and_27 (Z_FLAG_to_IR_ADDR_to_PC, A3, A2, not_38_out, not_39_out);
  or or_1 (R1_to_MEM_DATA, and_1_out, and_2_out);
  or or_2 (EN_REG_CLK, and_4_out, and_5_out, and_6_out, and_7_out);
  or or_3 (IR_ADDR_to_MEM_ADDR, and_9_out, and_10_out);
  or or_4 (EN_MEM, and_11_out, and_12_out, and_13_out, and_14_out);
  or or_5 (MEM_READ, and_15_out, and_16_out);
  or or_6 (MEM_DATA_to_REG_IN, and_17_out, and_18_out);
  or or_7 (RR3_to_MEM_ADDR, and_19_out, and_20_out);
  or or_8 (ALU_OUT_to_REG_IN, and_21_out, and_22_out, and_23_out, and_24_out);
  or or_9 (IR_ADDR_to_PC, and_25_out, and_26_out);
endmodule

module Instruction_Decoder__cont (
  input  A5,
  input  A4,
  input  A3,
  input  A2,
  input  A1,
  input  A0,
  output ALU_F3,
  output ALU_F2,
  output ALU_F1,
  output ALU_F0,
  output ALU_M,
  output ALU_C
);

  wire and_1_out, and_2_out, and_3_out, and_4_out, and_5_out, not_2_out, not_3_out, not_4_out, not_5_out,
       not_6_out, not_7_out, not_8_out, not_9_out, not_10_out;

  not not_1 (ALU_F3, A1);
  not not_2 (not_2_out, A2);
  not not_3 (not_3_out, A0);
  not not_4 (not_4_out, A2);
  not not_5 (not_5_out, A0);
  not not_6 (not_6_out, A3);
  not not_7 (not_7_out, A1);
  not not_8 (not_8_out, A1);
  not not_9 (not_9_out, A0);
  not not_10 (not_10_out, A2);
  and and_1 (and_1_out, A1, A0);
  not not_11 (ALU_C, A1);
  and and_2 (and_2_out, not_2_out, A0);
  and and_3 (and_3_out, A1, not_3_out);
  or or_1 (ALU_F1, not_4_out, not_5_out);
  and and_4 (and_4_out, not_6_out, not_7_out);
  and and_5 (and_5_out, not_8_out, not_9_out);
  or or_2 (ALU_M, not_10_out, and_1_out);
  or or_3 (ALU_F2, and_2_out, and_3_out);
  or or_4 (ALU_F0, and_4_out, and_5_out);
endmodule
