// Logisim project test 74181.circ as structural Verilog: 1 circuit, main circuit main
module main (
  input  [3:0] S,
  input  [3:0] A,
  input  [3:0] B,
  input  M,
  input  Cn,
  output G,
  output Cn_4,
  output P,
  output A_B,
  output [3:0] F
);

  wire n74181_1_cn_4, not_1_out;

  not not_1 (not_1_out, Cn);
  _74181 u_74181_1 (
    .S3(S[3]), .S2(S[2]), .S1(S[1]), .S0(S[0]), .B3(B[3]), .A3(A[3]), .B2(B[2]), .A2(A[2]), .B1(B[1]),
    .A1(A[1]), .B0(B[0]), .A0(A[0]), .M(M), .Cn(not_1_out), .G(G), .Cn_4(n74181_1_cn_4), .P(P), .F3(F[3]),
    .F2(F[2]), .A_B(A_B), .F1(F[1]), .F0(F[0]));
  not not_2 (Cn_4, n74181_1_cn_4);
endmodule
