// Logisim project test 8 bit 74181.circ as structural Verilog: 1 circuit, main circuit main
module main (
  input  [7:0] in_1,
  input  [7:0] in_2,
  input  [3:0] S,
  input  [7:0] A,
  input  M,
  input  Cn,
  input  [7:0] B,
  output G,
  output A__B,
  output Cn_4,
  output P,
  output A_B,
  output A_B_2,
  output A_B_3,
  output A__B_2,
  output [7:0] F,
  output G_2,
  output Cn_4_2,
  output P_2,
  output A_B_4
);

  wire n74181_1_p12, n74181_2_p12;
  wire [7:0] adder_1_out;

  // _74181 74181_1: pin names not known; wires that end beside it: B[3], A[3], B[2], A[2], B[1], A[1], B[0], A[0], M, Cn, G, n74181_1_p12, P, F[3], F[2], A_B_2, F[1], F[0]
  // _74181 74181_2: pin names not known; wires that end beside it: B[7], A[7], B[6], A[6], B[5], A[5], B[4], A[4], M, n74181_1_p12, G_2, n74181_2_p12, P_2, F[7], F[6], A_B_4, F[5], F[4]
  not not_1 (Cn_4, n74181_1_p12);
  not not_2 (Cn_4_2, n74181_2_p12);
  Adder adder_1 (.a(in_1), .b(in_2), .out(adder_1_out));  // open: cin, cout
  // Probe on adder_1_out
  and and_1 (A__B, n74181_2_p12, Cn);
  and and_2 (A_B, n74181_2_p12, ~Cn);  // AND_Gate
  and and_3 (A_B_3, ~n74181_2_p12, Cn);  // AND_Gate
  and and_4 (A__B_2, ~n74181_2_p12, ~Cn);  // AND_Gate

  // Notes on the sheet:
  //   LSB
  //   MSB
endmodule
